# Fritzing sketch esp 32 with soil moisture sensor (saved by Fritzing 0.9.3b)
breadboards: 1

parts:
  MH-ET_LIVE_ESP32_DEVKIT1 = MH-ET LIVE ESP32 DEVKIT 38 pins
  Part2 = Soil Moisture Sensor

nets:
  3V3: MH-ET_LIVE_ESP32_DEVKIT1.3V3, Part2.VCC
  N1: MH-ET_LIVE_ESP32_DEVKIT1.CMD, Part2.GND
  N2: MH-ET_LIVE_ESP32_DEVKIT1.IO15, Part2.SIG

notes:
  I've used pin number I015 on the esp32 module.

custom parts:
  MH-ET LIVE ESP32 DEVKIT 38 pins: http://mh.nodebb.com/topic/2/mh-et-live-esp32-devkit
