# Fritzing sketch esp32 with light sensor (saved by Fritzing 0.9.3b)
breadboards: 1

parts:
  MH-ET_LIVE_ESP32_DEVKIT1 = MH-ET LIVE ESP32 DEVKIT 38 pins
  Mod1 = KY-018 Photoresistor Module [package="Breakout board"]

nets:
  N1: MH-ET_LIVE_ESP32_DEVKIT1.CMD, Mod1.-
  5V: MH-ET_LIVE_ESP32_DEVKIT1.5V, Mod1.Vin
  N2: MH-ET_LIVE_ESP32_DEVKIT1.IO15, Mod1.S

custom parts:
  MH-ET LIVE ESP32 DEVKIT 38 pins: http://mh.nodebb.com/topic/2/mh-et-live-esp32-devkit
  KY-018 Photoresistor Module: KY-018 Photoresistor module, used to measure light intensity. It can determine the presence or absence of light.
