# Fritzing sketch raspberry pi pico interfaced with light sensor (saved by Fritzing 0.9.3b)
breadboards: 1

parts:
  Mod1 = Raspberry Pi Pico
  Mod2 = KY-018 Photoresistor Module [package="Breakout board"]

nets:
  N1: Mod1.pin_3, Mod1.pin_38, Mod1.pin_42, Mod2.-
  N2: Mod1.pin_7, Mod2.Vin
  N3: Mod1.pin_14, Mod2.S

custom parts:
  Raspberry Pi Pico: Raspberry Pi Pico. Based around the RP2040 microcontroller the Pico is a low cost microcontroller device bringing Raspberry Pi quality, cost, and easy of use to the microcontroller space. Jan 2021, Split part in to two versions: tht (this one) and SMD. This one will drill holes for a .1 in header in pcb to allow plugging in the module as well as providing pads to solder the module to the top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
  KY-018 Photoresistor Module: KY-018 Photoresistor module, used to measure light intensity. It can determine the presence or absence of light.
